# Fritzing sketch JP_MidTermPrj (saved by Fritzing 1.0.0rc)
breadboards: 1

parts:
  A1 = Particle - Photon2  # not connected
  U1 = ENCODER_RGB [package=encoder_led_2]  # not connected
  R1 = Resistor [tolerance=±5% power=0.25W resistance=220 package=THT]
  R3 = Resistor [tolerance=±5% power=0.25W resistance=220 package=THT]
  S1 = Pushbutton [package="[THT]"]
  OLED_I2C1 = OLED 128x64 I2C Monochrome Display  # not connected
  Neopixel4 = Adafruit RBG Smart Neopixel [package="DIP (Dual Inline) [THT]"]  # not connected
  S2 = Pushbutton [package="[THT]"]

nets:
  N1: R1.Pin_0, S2.Pin_3, S2.Pin_4
  N2: R1.Pin_1, R3.Pin_1
  N3: R3.Pin_0, S1.Pin_3, S1.Pin_4
  N4: S1.Pin_1, S1.Pin_2
  N5: S2.Pin_1, S2.Pin_2

custom parts:
  Particle - Photon2: The Photon 2 is a microcontroller and Wi-Fi networking developed by particle. Features: 802.11a/b/g/n Wi-Fi, 2.4 GHz and 5 GHz Integrated PCB antenna Integrated U.FL connector for external antenna Integrated RF switch BLE 5 using same antenna as Wi-Fi Realtek RTL8721DM MCU ARM Cortex M33 CPU, 200 MHz 2048 KB (2 MB) user application maximum size 3072 KB (3 MB) of RAM available to user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
  ENCODER_RGB: SparkFun RGB rotary Encoder
  Pushbutton: A generic pushbutton.
